# Fritzing sketch design (saved by Fritzing 0.9.5d)
breadboards: 1

parts:
  Part1 = Arduino Uno (Rev3) - ICSP
  S1 = Pushbutton [package="[THT]"]
  S2 = Pushbutton [package="[THT]"]
  R1 = Resistor [tolerance=±5% resistance=220 package=THT]
  R2 = Resistor [tolerance=±5% resistance=220 package=THT]
  K1 = G3VM-61E1 [package=g3vm-61e1]
  M1 = DC Motor
  K2 = G3VM-61E1 [package=g3vm-61e1]
  J1 = Power Jack [package=power_jack_pth]
  J2 = screw terminal, 3 pins
  J3 = screw terminal, 3 pins
  U1 = mystery part, 3 pins [chip_label="Reed Switch"]

nets:
  N1: Part1.D8, K2.P$4
  N2: Part1.D10_PWM/SS, K1.P$4
  N3: Part1.D2, U1.pin1
  N4: Part1.D3_PWM, S1.Pin_1, S1.Pin_2, R1.Pin_0
  N5: Part1.D4, S2.Pin_1, S2.Pin_2, R2.Pin_0
  N6: Part1.5V, S1.Pin_3, S1.Pin_4, S2.Pin_3, S2.Pin_4, K1.P$5, K2.P$5, K2.P$6, U1.pin3
  N7: Part1.GND, R1.Pin_1, K1.P$6, U1.pin2
  N8: K1.P$1, J3.pin2
  N9: K1.P$2, M1.pin_1
  N10: K1.P$3, J2.pin1
  N11: M1.pin_2, K2.P$2
  N12: K2.P$1, J3.pin3
  N13: K2.P$3, J2.pin2
  N14: J1.GND, J2.pin3
  N15: J1.GNDBREAK, J3.pin1

notes:
  Open
  Close
  12v
  NC
  NO
  COM
  S
  +
  -
  JQC-3FF-S-Z
